# Fritzing sketch arduino Sketch (saved by Fritzing 0.9.3b)
breadboards: 2

parts:
  Componente3 = Arduino Mega 2560 (Rev3)
  LCD1 = 20x4 LCD display [part_number=2004A]
  R1 = TRIMPOT [package=3386u]
  Componente4 = RFID-RC522-v2
  Componente6 = Real Time Clock Module - DS1307 RTC Breakout Board
  J1 = Piezo Speaker
  LED2 = smd LED [color="Red (633nm)" package="0805 [SMD]"]
  R3 = Resistor [tolerance=±5% resistance=220 package="0603 [SMD]"]
  LED3 = smd LED [color="Red (633nm)" package="0805 [SMD]"]
  R4 = Resistor [tolerance=±5% resistance=220 package="0603 [SMD]"]

nets:
  N1: Componente3.D21/SCL, Componente6.SCL
  N2: Componente3.D20/SDA, Componente6.SDA
  N3: Componente3.D15/RX3, LED3.anode, R4.Pin_0, R4.Pin_1
  N4: Componente3.D14/TX3, LED2.anode, R3.Pin_0, R3.Pin_1
  GND: Componente3.GND, LCD1.Vss, LCD1.R/W, LCD1.K_-, R1.CCW, Componente4.GND, Componente6.GND, J1.pin1, LED2.cathode, LED3.cathode
  N5: Componente3.D12_PWM, LCD1.RS
  N6: Componente3.D11_PWM, LCD1.E
  N7: Componente3.D8_PWM, J1.pin2
  3V3: Componente3.3V3, Componente4.3.3V
  5V: Componente3.5V, LCD1.Vdd, LCD1.A_+, R1.CW, Componente6.5V
  N8: Componente3.D2_PWM, LCD1.DB7
  N9: Componente3.D3_PWM, LCD1.DB6
  N10: Componente3.D4_PWM, LCD1.DB5
  N11: Componente3.D5_PWM, LCD1.DB4
  N12: Componente3.D22, Componente4.RST
  N13: Componente3.D50, Componente4.MISO
  N14: Componente3.D51, Componente4.MOSI
  N15: Componente3.D52, Componente4.SCK
  N16: Componente3.D53, Componente4.SDA
  N17: LCD1.Vo, R1.WIPER

custom parts:
  20x4 LCD display: 20x4 character display. CHECK LED POLARITY BEFORE CONNECTING POWER Some versions of the dispaly have the polarity of the LED pins "A" and "K" reversed.
  RFID-RC522-v2: A simple China made RFID-RC522 Reader; do check the pin labels, as this is a MFRC522 based clone.
